// Logisim project lab2.circ as structural Verilog: 1 circuit, main circuit 四位二进制可逆计数器
module \四位二进制可逆计数器  (
  input  in_1,
  input  in_2,
  input  in_3,
  output out_4,
  output out_5,
  output out_6,
  output out_7
);


  // Other names for the same wires on the sheet: CLR = in_2; CPD = in_3; CPU = in_1; SA = out_7; SB = out_6;
  //   SC = out_5; SD = out_4
endmodule
